# Fritzing sketch Schematic (saved by Fritzing 0.9.3b)
breadboards: 1

parts:
  Mod1 = Raspberry Pi 4B
  R1 = Resistor [tolerance=±0.5% resistance=330 package=THT]
  LED1 = LED - 5mm [color="Green (555nm)" package="5 mm [THT]"]
  HC-SR04_Sensor_1 = HC-SR04 Ultrasonic Distance Sensor
  R2 = Resistor [tolerance=±5% resistance=330 package=THT]
  R3 = Resistor [tolerance=±5% resistance=440 package=THT]

nets:
  5V: Mod1.5V, HC-SR04_Sensor_1.VCC
  GND: Mod1.GND, LED1.cathode, HC-SR04_Sensor_1.GND, R3.Pin_0
  N1: Mod1.GPIO17, R1.Pin_1
  N2: Mod1.GPIO25, HC-SR04_Sensor_1.TRIG
  N3: Mod1.GPIO16, R2.Pin_1, R3.Pin_1
  N4: R1.Pin_0, LED1.anode
  N5: HC-SR04_Sensor_1.ECHO, R2.Pin_0

notes:
  Pin 11
  Pin 22
  Pin 36
  5 V
  GND
  440 Ohm
  330 Ohm
  Trig -> 3.3 V input to Sensor from RasPi
  - Trigger to send sound waves
  Echo -> 5 V Output to RasPi
  - This is converted to < 3.3 V by voltage divider (GPIO Max Voltage should be < 3.3 )
  - Time duration of echo gives the object distance
